# Fritzing sketch Esquema Robot (saved by Fritzing 0.9.2b)
breadboards: 1

parts:
  Raspberry_Pi_A+ = Raspberry Pi B+
  J1 = Screw terminal - 2 pins [package=THT]
  J2 = Screw terminal - 2 pins [package=THT]
  J3 = Screw terminal - 2 pins [package=THT]
  J4 = Screw terminal - 2 pins [package=THT]
  J7 = female pin header, 3 pins [form="♀ (female)"]
  Funduino_Pro_Mini = Arduino Pro Mini v13
  J8 = female pin header, 4 pins [form="♀ (female)"]
  R1 = Resistor [tolerance=±5% resistance=1k package=THT]
  R2 = Resistor [tolerance=±5% resistance=1k package=THT]
  J9 = Screw terminal - 2 pins [package=THT]

nets:
  N1: Raspberry_Pi_A+.GPIO20, J4.pin2
  N2: Raspberry_Pi_A+.GPIO16, J4.pin1
  N3: Raspberry_Pi_A+.GPIO7, J1.pin2
  N4: Raspberry_Pi_A+.GPIO8, J3.pin2
  N5: Raspberry_Pi_A+.GPIO25, J3.pin1
  GND: Raspberry_Pi_A+.GND, J7.pin3, Funduino_Pro_Mini.GND, J8.pin1, R1.Pin_0, J9.pin1
  N6: Raspberry_Pi_A+.GPIO24, J2.pin2
  N7: Raspberry_Pi_A+.GPIO23, J2.pin1
  N8: Raspberry_Pi_A+.GPIO18, J1.pin1
  N9: Raspberry_Pi_A+.GPIO15, Funduino_Pro_Mini.D0/TX
  N10: Raspberry_Pi_A+.GPIO14, Funduino_Pro_Mini.D1/RX
  N11: Raspberry_Pi_A+.5V, J7.pin1, Funduino_Pro_Mini.RAW, J8.pin4
  N12: J7.pin2, Funduino_Pro_Mini.D2
  N13: Funduino_Pro_Mini.D4, R1.Pin_1, R2.Pin_1
  N14: Funduino_Pro_Mini.D3_PWM, J8.pin3
  N15: J8.pin2, R2.Pin_0

notes:
  Motor Front Left
  Motor Front Right
  Motor Back Left
  Motor Back Right
  Servo
  A_IA
  A_IB
  B_IB
  B_IA
  5V
  GND
  HC-SR04
  TRIG
  ECHO
  Motor Drives
